// Logisim project mapa.circ as structural Verilog: 1 circuit, main circuit main
module main (
);

  wire and_1_out, and_2_out, or_1_out, undriven, undriven_2, undriven_3, undriven_4;

  Clock clock_1 ();  // open: out
  and and_1 (and_1_out, undriven_2, undriven_4);
  and and_2 (and_2_out, undriven_4, undriven_3);
  or or_1 (or_1_out, undriven, and_2_out, and_1_out);
  _7_Segment_Display u_7_segment_display_1 ();  // open: g, f, a, b, e, d, c, dp
endmodule
