// Logisim project mapa2.circ as structural Verilog: 11 circuits, main circuit main
module main (
  input  [3:0] \input 
);

  wire clock_1_out, d_ff_1_q, LogicaEstados_ja, LogicaEstados_jb, LogicaEstados_jc, LogicaEstados_jd,
       LogicaEstados_ka, LogicaEstados_kb, LogicaEstados_kc, LogicaEstados_kd, LogicaSalida_out_2,
       LogicaSalida_out_3, LogicaSalida_out_4, LogicaSalida_out_5, LogicaSalida_out_6, LogicaSalida_out_7,
       LogicaSalida_out_8;
  wire [3:0] FFJK_out_9;

  Clock clock_1 (.out(clock_1_out));
  D_Flip_Flop d_ff_1 (.clk(clock_1_out), .D(1'b1), .Q(d_ff_1_q));  // open: Qn, preset, en, reset
  LogicaEstados LogicaEstados (
    .\input (\input ), .estado(FFJK_out_9), .cambio(d_ff_1_q), .Ja(LogicaEstados_ja), .Ka(LogicaEstados_ka),
    .Jb(LogicaEstados_jb), .Kb(LogicaEstados_kb), .Jc(LogicaEstados_jc), .Kc(LogicaEstados_kc),
    .Jd(LogicaEstados_jd), .Kd(LogicaEstados_kd));
  FFJK FFJK (
    .Jd(LogicaEstados_jd), .Kd(LogicaEstados_kd), .Jc(LogicaEstados_jc), .Kc(LogicaEstados_kc),
    .Kb(LogicaEstados_kb), .Jb(LogicaEstados_jb), .Ka(LogicaEstados_ka), .Ja(LogicaEstados_ja),
    .out_9(FFJK_out_9));
  LogicaSalida LogicaSalida (
    .in_1(FFJK_out_9), .out_2(LogicaSalida_out_2), .out_3(LogicaSalida_out_3), .out_4(LogicaSalida_out_4),
    .out_5(LogicaSalida_out_5), .out_6(LogicaSalida_out_6), .out_7(LogicaSalida_out_7),
    .out_8(LogicaSalida_out_8));
  _7_Segment_Display u_7_segment_display_1 (
    .g(LogicaSalida_out_8), .f(LogicaSalida_out_7), .a(LogicaSalida_out_2), .b(LogicaSalida_out_3),
    .e(LogicaSalida_out_6), .d(LogicaSalida_out_5), .c(LogicaSalida_out_4));  // open: dp
endmodule

module FFJK (
  input  Ja,
  input  Ka,
  input  Jb,
  input  Kb,
  input  Jc,
  input  Kc,
  input  Jd,
  input  Kd,
  output [3:0] out_9
);

  wire clock_1_out;

  Clock clock_1 (.out(clock_1_out));
  J_K_Flip_Flop A (.J(Ja), .clk(clock_1_out), .K(Ka), .Q(out_9[0]));  // open: Qn, preset, en, reset
  J_K_Flip_Flop B (.J(Jb), .clk(clock_1_out), .K(Kb), .Q(out_9[1]));  // open: Qn, preset, en, reset
  J_K_Flip_Flop C (.J(Jc), .clk(clock_1_out), .K(Kc), .Q(out_9[2]));  // open: Qn, preset, en, reset
  J_K_Flip_Flop D (.J(Jd), .clk(clock_1_out), .K(Kd), .Q(out_9[3]));  // open: Qn, preset, en, reset
endmodule

module LogicaSalida (
  input  [3:0] in_1,
  output out_2,
  output out_3,
  output out_4,
  output out_5,
  output out_6,
  output out_7,
  output out_8
);

  SalidaA a (.in_1(in_1), .Sa(out_2));
  SalidaB b (.in_1(in_1), .Sb(out_3));
  SalidaC c (.in_1(in_1), .Sc(out_4));
  SalidaD d (.in_1(in_1), .Sd(out_5));
  SalidaE e (.in_1(in_1), .Se(out_6));
  SalidaF f (.in_1(in_1), .Sf(out_7));
  SalidaG g (.in_1(in_1), .Sg(out_8));
endmodule

module LogicaEstados (
  input  [3:0] \input ,
  input  [3:0] estado,
  input  cambio,
  output Ja,
  output Ka,
  output Jb,
  output Kb,
  output Jc,
  output Kc,
  output Jd,
  output Kd
);

  wire BC_out, BD_out, CD_2_out, CD_out, minus_A_B_out, minus_AB_out, minus_AC_out, not_1_out, not_2_out,
       not_3_out;
  wire [2:0] multiplexer_1_out;

  Multiplexer #(.width(4)) multiplexer_1 (
    .in0(\input ), .in1(estado), .out({Jb, multiplexer_1_out}), .sel(cambio));  // open: en
  not not_1 (not_1_out, multiplexer_1_out[0]);
  not not_2 (not_2_out, multiplexer_1_out[1]);
  not not_3 (not_3_out, multiplexer_1_out[2]);
  and BD (BD_out, multiplexer_1_out[1], Jb);
  and BC (BC_out, multiplexer_1_out[2], Jb);
  and BCD (Ka, multiplexer_1_out[1], multiplexer_1_out[2], Jb);
  and CD (CD_out, multiplexer_1_out[2], Jb);
  and minus_AC (minus_AC_out, not_1_out, multiplexer_1_out[2]);
  and AD (Jc, multiplexer_1_out[0], Jb);
  and minus_AB (minus_AB_out, not_1_out, multiplexer_1_out[1]);
  and CD_2 (CD_2_out, multiplexer_1_out[2], Jb);
  and minus_A_B (minus_A_B_out, not_1_out, not_2_out);
  or BD___BC (Ja, BD_out, BC_out);
  or CD____AC (Kb, CD_out, minus_AC_out);
  or minus_AB___CD (Kc, minus_AB_out, CD_2_out);
  or A____A_B____C (Jd, multiplexer_1_out[0], minus_A_B_out, not_3_out);
  or A____A_B___C (Kd, multiplexer_1_out[0], minus_A_B_out, multiplexer_1_out[2]);
endmodule

module SalidaA (
  input  [3:0] in_1,
  output Sa
);

  wire B_C_out, minus_BCD_out, minus_C_D_out, not_1_out, not_2_out, not_3_out;

  not not_1 (not_1_out, in_1[2]);
  not not_2 (not_2_out, in_1[3]);
  not not_3 (not_3_out, in_1[1]);
  and minus_C_D (minus_C_D_out, not_1_out, not_2_out);
  and B_C (B_C_out, in_1[1], not_1_out);
  and minus_BCD (minus_BCD_out, not_3_out, in_1[2], in_1[3]);
  or or_1 (Sa, in_1[0], minus_C_D_out, B_C_out, minus_BCD_out);
endmodule

module SalidaB (
  input  [3:0] in_1,
  output Sb
);

  wire AB_out, AD_out, BD_out, C_D_out, minus_A_B_C_out, not_1_out, not_2_out, not_3_out, not_4_out;

  not not_1 (not_1_out, in_1[0]);
  not not_2 (not_2_out, in_1[1]);
  not not_3 (not_3_out, in_1[2]);
  not not_4 (not_4_out, in_1[3]);
  and minus_A_B_C (minus_A_B_C_out, not_1_out, not_2_out, not_3_out);
  and BD (BD_out, in_1[1], in_1[3]);
  and AD (AD_out, in_1[0], in_1[3]);
  and AB (AB_out, in_1[0], in_1[1]);
  and C_D (C_D_out, in_1[2], not_4_out);
  or or_1 (Sb, minus_A_B_C_out, BD_out, AD_out, AB_out, C_D_out);
endmodule

module SalidaC (
  input  [3:0] in_1,
  output Sc
);

  or or_1 (Sc, in_1[0], in_1[1], in_1[2], in_1[3]);
endmodule

module SalidaD (
  input  [3:0] in_1,
  output Sd
);

  wire A_B_C_out, AC_D_out, minus_A_BCD_out, minus_A_C_D_out, not_1_out, not_2_out, not_3_out, not_4_out;

  not not_1 (not_1_out, in_1[0]);
  not not_2 (not_2_out, in_1[2]);
  not not_3 (not_3_out, in_1[3]);
  not not_4 (not_4_out, in_1[1]);
  and minus_A_C_D (minus_A_C_D_out, not_1_out, not_2_out, not_3_out);
  and A_B_C (A_B_C_out, in_1[0], not_4_out, not_2_out);
  and minus_A_BCD (minus_A_BCD_out, not_1_out, not_4_out, in_1[2], in_1[3]);
  and AC_D (AC_D_out, in_1[0], in_1[2], not_3_out);
  or or_1 (Sd, minus_A_C_D_out, A_B_C_out, minus_A_BCD_out, AC_D_out);
endmodule

module SalidaE (
  input  [3:0] in_1,
  output Se
);

  wire AC_D_out, minus_B_C_D_out, not_1_out, not_2_out, not_3_out;

  not not_1 (not_1_out, in_1[3]);
  not not_2 (not_2_out, in_1[1]);
  not not_3 (not_3_out, in_1[2]);
  and AC_D (AC_D_out, in_1[0], in_1[2], not_1_out);
  and minus_B_C_D (minus_B_C_D_out, not_2_out, not_3_out, not_1_out);
  or or_1 (Se, AC_D_out, minus_B_C_D_out);
endmodule

module SalidaF (
  input  [3:0] in_1,
  output Sf
);

  wire A_D_out, B_D_out, BC_out, minus_A_BD_out, not_1_out, not_2_out, not_3_out;

  not not_1 (not_1_out, in_1[0]);
  not not_2 (not_2_out, in_1[1]);
  not not_3 (not_3_out, in_1[3]);
  and minus_A_BD (minus_A_BD_out, not_1_out, not_2_out, in_1[3]);
  and B_D (B_D_out, in_1[1], not_3_out);
  and A_D (A_D_out, in_1[0], not_3_out);
  and BC (BC_out, in_1[1], in_1[2]);
  or or_1 (Sf, minus_A_BD_out, B_D_out, A_D_out, BC_out);
endmodule

module SalidaG (
  input  [3:0] in_1,
  output Sg
);

  wire A_D_out, BC_out, minus_A_BD_out, minus_B_C_out, minus_C_D_out, not_1_out, not_2_out, not_3_out,
       not_4_out;

  not not_1 (not_1_out, in_1[0]);
  not not_2 (not_2_out, in_1[1]);
  not not_3 (not_3_out, in_1[3]);
  not not_4 (not_4_out, in_1[2]);
  and minus_A_BD (minus_A_BD_out, not_1_out, not_2_out, in_1[3]);
  and A_D (A_D_out, in_1[0], not_3_out);
  and minus_B_C (minus_B_C_out, not_2_out, not_4_out);
  and BC (BC_out, in_1[0], in_1[2]);
  and minus_C_D (minus_C_D_out, not_4_out, not_3_out);
  or or_1 (Sg, minus_A_BD_out, A_D_out, minus_B_C_out, BC_out, minus_C_D_out);
endmodule
